# Fritzing sketch startkit_led (saved by Fritzing 0.9.3b)
circuit board: 8.46667cm x 5.64444cm
breadboards: 1

parts:
  S1 = Pushbutton [package="[THT]"]
  Part1 = Arduino Nano (Rev3.0)
  LED1 = RGB LED (com. cathode, rgb) [package="5 mm [THT]"]
  LED2 = RGB LED (com. cathode, rgb) [package="5 mm [THT]"]
  C1 = Electrolytic Capacitor [capacitance=220µF package="100 mil [THT, electrolytic]"]

nets:
  N1: S1.Pin_1, S1.Pin_2, S1.Pin_3, S1.Pin_4, Part1.D4, Part1.GND, LED1.common_cathode, LED2.common_cathode, C1.-
  N2: Part1.D5, LED1.blue_anode
  N3: Part1.VIN, LED1.green_anode, LED2.green_anode, C1.+
  N4: LED1.red_anode, LED2.blue_anode
